# Fritzing sketch dht22_raspberrypi_3 (saved by Fritzing 0.9.3b)
breadboards: 1

parts:
  PiDi_Scoutlab_DHT22_Platine1 = Scoutlab DHT22 Platine [part_number=Scoutlab package=Scoutlab]
  Raspberry_Pi_1 = Raspberry Pi 3 [part_number=RPI-3-V1.2]

nets:
  N1: PiDi_Scoutlab_DHT22_Platine1.Data, Raspberry_Pi_1.GPIO21
  VCC: PiDi_Scoutlab_DHT22_Platine1.VCC, Raspberry_Pi_1.3v3
  GND: PiDi_Scoutlab_DHT22_Platine1.GND, Raspberry_Pi_1.GND

custom parts:
  Scoutlab DHT22 Platine: Scoutlab DHT22
